# Fritzing sketch HapEMSG REV2 (saved by Fritzing 0.9.3b)
circuit board: 11.4391cm x 5.28029cm
breadboards: 2

parts:
  Part1 = Adafruit HUZZAH32 ESP32 Feather [part_number="Adafruit #3405"]
  Part2 = Adafruit MicroSD card breakout board [part_number="Adafruit #254"]
  IRFB2 = IRFB4020
  IRFB3 = IRFB4020
  IRFB4 = IRFB4020
  X9C102P2 = X9C102P
  APV1 = APV122 [package="DIP (Dual Inline) [THT]"]
  APV2 = APV122 [package="DIP (Dual Inline) [THT]"]
  LH1 = LH1546 [package="DIP (Dual Inline) [THT]"]
  LH2 = LH1546 [package="DIP (Dual Inline) [THT]"]
  LH3 = LH1546 [package="DIP (Dual Inline) [THT]"]
  LH4 = LH1546 [package="DIP (Dual Inline) [THT]"]
  R1 = Resistor [tolerance=±5% resistance=220 package=THT]
  R2 = Resistor [tolerance=±5% resistance=220 package=THT]
  R3 = Resistor [tolerance=±5% resistance=220 package=THT]
  R4 = Resistor [tolerance=±5% resistance=220 package=THT]
  R5 = Resistor [tolerance=±5% resistance=1M package=THT]
  C1 = Tantalum Capacitor [capacitance=0.1µF package="100 mil [THT, tantalum]"]
  R6 = Resistor [tolerance=±5% resistance=1M package=THT]
  C2 = Tantalum Capacitor [capacitance=0.1µF package="100 mil [THT, tantalum]"]
  C3 = Tantalum Capacitor [capacitance=10µF package="100 mil [THT, tantalum]"]
  IRFB5 = IRFB4020
  JP1 = Header 12 [package=1x12_machine-pin-header_lock.004]
  X9C102P1 = X9C102P

nets:
  N1: Part1.IO21, X9C102P1.U/D
  N2: Part1.IO16, Part2.CS
  N3: Part1.MISO, Part2.DO
  N4: Part1.MOSI, Part2.DI
  N5: Part1.SCK, Part2.CLK
  N6: Part1.A5_IO4, X9C102P1.INC
  N7: Part1.A3_I39, JP1.12
  N8: Part1.A2_I34, APV2.pin1, X9C102P1.VW/RW
  N9: Part1.A1_DAC1, X9C102P2.VW/RW, APV1.pin1
  N10: Part1.A0_DAC2, X9C102P1.CS
  GND: Part1.GND, Part2.GND, X9C102P2.VSS, X9C102P2.VL/RL, APV1.pin2, APV2.pin2, LH1.pin2, LH2.pin2, LH3.pin2, LH4.pin2, C3.-, JP1.11, X9C102P1.VSS, X9C102P1.VL/RL
  VCC: Part1.3.3V, Part2.+3V3, X9C102P2.VH/RH, X9C102P2.VCC, C3.+, JP1.10, X9C102P1.VH/RH, X9C102P1.VCC
  N11: Part1.IO12_A11, X9C102P2.U/D
  N12: Part1.IO27_A10, X9C102P2.INC
  N13: Part1.IO33_A9, X9C102P2.CS
  N14: Part1.IO15_A8, R1.Pin_1, R2.Pin_0
  N15: Part1.IO14_A6, R3.Pin_1, R4.Pin_0
  N16: IRFB2.gate, IRFB4.gate, APV2.pin6, C1.-, R6.Pin_0
  N17: IRFB2.drain, LH4.pin3, JP1.8
  N18: IRFB2.source, IRFB4.source, APV2.pin4, C1.+, R6.Pin_1
  N19: IRFB3.gate, APV1.pin6, R5.Pin_1, C2.-, IRFB5.gate
  N20: IRFB3.drain, LH2.pin3, JP1.4
  N21: IRFB3.source, APV1.pin4, R5.Pin_0, C2.+, IRFB5.source
  N22: IRFB4.drain, LH3.pin4, JP1.5
  N23: LH1.pin1, R1.Pin_0
  N24: LH1.pin3, JP1.2
  N25: LH1.pin4, IRFB5.drain, JP1.1
  N26: LH2.pin1, R2.Pin_1
  N27: LH2.pin4, JP1.3
  N28: LH3.pin1, R3.Pin_0
  N29: LH3.pin3, JP1.6
  N30: LH4.pin1, R4.Pin_1
  N31: LH4.pin4, JP1.7

notes:
  ariza@informatik.uni-hamburg.de
  HapEMS HCI UHH 2019

custom parts:
  Adafruit MicroSD card breakout board: Not just a simple breakout board, this microSD adapter goes the extra mile - designed for ease of use. Onboard 5v->3v regulator provides 150mA for power-hungry cards 3v level shifting means you can use this with ease on either 3v or 5v systems Uses a proper level shifting chip, not resistors: less problems, and faster read/write access Use 3 or 4 digital pins to read and write 2Gb+ of storage!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
  IRFB4020: IRFB4020 https://www.infineon.com/dgdl/irfb4020pbf.pdf?fileId=5546d462533600a4015356158ffd1e05
  X9C102P: X9C102P https://www.renesas.com/us/en/www/doc/datasheet/x9c102-103-104-503.pdf
  APV122: APV122 https://www.mouser.de/datasheet/2/315/semi_eng_apv-1304993.pdf
