# Fritzing sketch HapFingers REV4 (saved by Fritzing 0.9.3b)
circuit board: 11.68cm x 6.63555cm
breadboards: 2

parts:
  R2 = Resistor [tolerance=±5% resistance=1k package=THT]
  R5 = Resistor [tolerance=±5% resistance=3.3k package=THT]
  C3 = Tantalum Capacitor [capacitance=10µF package="100 mil [THT, tantalum]"]
  JP1 = Header 12 [package=1x12_machine-pin-header_lock.004]
  Part4 = Adafruit MAX98357A I2S 3W Class D Amplifier [part_number="Adafruit #3006"]
  Q1 = TIP120 Hi-Current Darlington Transistor
  JP2 = Header 2 [package=molex-1x2_lock]
  D2 = Rectifier Diode [part_number=1N4001 package="300 mil [THT]"]
  Q2 = TIP120 Hi-Current Darlington Transistor
  R7 = Resistor [tolerance=±5% resistance=1k package=THT]
  D3 = Rectifier Diode [part_number=1N4001 package="300 mil [THT]"]
  JP5 = Header 4 [package=molex-1x4_lock]
  JP6 = Header 4 [package=molex-1x4_lock]
  Part1 = Adafruit HUZZAH32 ESP32 Feather [part_number="Adafruit #3405"]
  Part5 = Adafruit MAX98357A I2S 3W Class D Amplifier [part_number="Adafruit #3006"]
  JP3 = Header 12 [package=1x12_machine-pin-header_lock.004]
  R8 = Resistor [tolerance=±5% resistance=3.3k package=THT]
  Q3 = TIP120 Hi-Current Darlington Transistor
  D4 = Rectifier Diode [part_number=1N4001 package="300 mil [THT]"]
  R9 = Resistor [tolerance=±5% resistance=1k package=THT]
  Part3 = Adafruit CAP1188 - 8-Key Capacitive Touch Sensor Breakout [part_number="Adafruit #1602"]
  Part2 = Adafruit MicroSD card breakout board [part_number="Adafruit #254"]

nets:
  GND: R2.Pin_0, R5.Pin_1, C3.-, Part4.GND, Part4.GAIN, Q1.EMITTER, JP2.1, Q2.EMITTER, R7.Pin_0, JP5.3, Part1.GND, Part5.GND, Part5.GAIN, R8.Pin_1, Q3.EMITTER, R9.Pin_0, Part3.GND, Part2.GND
  N1: R2.Pin_1, Q1.BASE, Part1.IO27_A10
  N2: R5.Pin_0, JP1.12, Part1.A4_IO36
  VIN: C3.+, JP1.11, Part4.VIN, JP5.4, Part1.VBAT, Part5.VIN, JP3.12
  N3: JP1.1, JP1.3, JP2.2, D2.cathode, D3.cathode, JP3.10, D4.cathode
  N4: JP1.2, Q1.COLLECTOR, D2.anode
  N5: JP1.4, Q2.COLLECTOR, D3.anode
  N6: JP1.5, JP6.1
  N7: JP1.6, JP6.4
  N8: JP1.7, Part5.VO+
  N9: JP1.8, Part5.VO-
  N10: JP1.9, Part4.VO-
  N11: JP1.10, Part4.VO+
  N12: Part4.DIN, Part1.A0_DAC2
  N13: Part4.BCLK, Part1.IO14_A6
  N14: Part4.LRCLK, Part1.SCL
  N15: Q2.BASE, R7.Pin_1, Part1.IO12_A11
  N16: JP5.1, Part1.IO21, Part3.SDA/MISO
  N17: JP5.2, Part1.SDA, Part3.SCK
  N18: Part1.IO16, Part2.CS
  N19: Part1.MISO, Part2.DO
  N20: Part1.MOSI, Part2.DI
  N21: Part1.SCK, Part2.CLK
  N22: Part1.A3_I39, JP3.11, R8.Pin_0
  N23: Part1.A1_DAC1, Part5.DIN
  3.3V: Part1.3.3V, Part3.VIN, Part2.+3V3
  N24: Part1.IO33_A9, Q3.BASE, R9.Pin_1
  N25: Part1.IO15_A8, Part5.BCLK
  N26: Part1.IO32_A7, Part5.LRCLK
  N27: JP3.1, Part3.CS8
  N28: JP3.2, Part3.CS7
  N29: JP3.3, Part3.CS6
  N30: JP3.4, Part3.CS5
  N31: JP3.5, Part3.CS4
  N32: JP3.6, Part3.CS3
  N33: JP3.7, Part3.CS2
  N34: JP3.8, Part3.CS1
  N35: JP3.9, Q3.COLLECTOR, D4.anode

notes:
  HapFingers HCI UHH 2019
  ariza@informatik.uni-hamburg.de

custom parts:
  Adafruit MAX98357A I2S 3W Class D Amplifier: Listen to this good news - we now have an all in one digital audio amp breakout board that works incredibly well with the Raspberry Pi! If you're looking for an easy and low cost way to get you digital sound files bumpin' then the MAX08357 I2S Amp Breakout is for you. It takes standard I2S digital audio input and, not only decodes it into analog, but also amplifies it directly into a speaker.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
  Adafruit CAP1188 - 8-Key Capacitive Touch Sensor Breakout: Add lots of touch sensors to your next microcontroller project with this easy-to-use 8-channel capacitive touch sensor breakout board, starring the CAP1188. This chip can handle up to 8 individual touch pads, and has a very nice feature that makes it stand out for us: it will light up the 8 onboard LEDs when the matching touch sensor fires to help you debug your sensor setup. The CAP1188 has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
  Adafruit MicroSD card breakout board: Not just a simple breakout board, this microSD adapter goes the extra mile - designed for ease of use. Onboard 5v->3v regulator provides 150mA for power-hungry cards 3v level shifting means you can use this with ease on either 3v or 5v systems Uses a proper level shifting chip, not resistors: less problems, and faster read/write access Use 3 or 4 digital pins to read and write 2Gb+ of storage!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
